# Fritzing sketch project (saved by Fritzing 0.9.3b)
breadboards: 1

parts:
  S1 = Pushbutton [package="[THT]"]
  S2 = Pushbutton [package="[THT]"]
  S3 = Pushbutton [package="[THT]"]
  S4 = Pushbutton [package="[THT]"]
  S5 = Pushbutton [package="[THT]"]
  S6 = Pushbutton [package="[THT]"]
  S7 = Pushbutton [package="[THT]"]
  S8 = Pushbutton [package="[THT]"]
  부품1 = Arduino Uno (Rev3)
  R1 = Rotary Potentiometer (Small) [maximum_resistance=100kΩ package=THT]
  J1 = Piezo Speaker
  LED4 = LED - 5mm [color="Orange (620nm)" package="5 mm [THT]"]
  LED5 = LED - 5mm [color="Yellow (595nm)" package="5 mm [THT]"]
  LED6 = LED - 5mm [color="Red (633nm)" package="5 mm [THT]"]
  R3 = Resistor [tolerance=±5% resistance=1k package=THT]
  R4 = Resistor [tolerance=±5% resistance=1k package=THT]
  R2 = Resistor [tolerance=±5% resistance=1k package=THT]
  LCD1 = LCD screen  # not connected

nets:
  N1: S1.Pin_1, S1.Pin_2, S2.Pin_1, S2.Pin_2, S3.Pin_1, S3.Pin_2, S4.Pin_1, S4.Pin_2, S5.Pin_1, S5.Pin_2, S6.Pin_1, S6.Pin_2, S7.Pin_1, S7.Pin_2, S8.Pin_1, S8.Pin_2, 부품1.GND, R1.leg1, J1.pin1, R3.Pin_1, R4.Pin_1, R2.Pin_1
  N2: S1.Pin_3, S1.Pin_4, 부품1.D13/SCK
  N3: S2.Pin_3, S2.Pin_4, 부품1.D12/MISO
  N4: S3.Pin_3, S3.Pin_4, 부품1.D11_PWM/MOSI
  N5: S4.Pin_3, S4.Pin_4, 부품1.D10_PWM/SS
  N6: S5.Pin_3, S5.Pin_4, 부품1.D9_PWM
  N7: S6.Pin_3, S6.Pin_4, 부품1.D8
  N8: S7.Pin_3, S7.Pin_4, 부품1.D7
  N9: S8.Pin_3, S8.Pin_4, 부품1.D6_PWM
  N10: 부품1.A0, R1.wiper
  N11: 부품1.D2, LED6.anode
  N12: 부품1.D3_PWM, LED5.anode
  N13: 부품1.D4, LED4.anode
  N14: 부품1.D5_PWM, J1.pin2
  N15: 부품1.5V, R1.leg2
  N16: LED4.cathode, R2.Pin_0
  N17: LED5.cathode, R3.Pin_0
  N18: LED6.cathode, R4.Pin_0
